// Logisim project Schéma_logique_3_capteurs.circ as structural Verilog: 1 circuit, main circuit main
module main (
  input  in_1,
  input  in_2,
  input  in_3,
  output Flan_Droit,
  output Random,
  output Flan_gauche
);

  wire and_1_out, and_2_out, and_3_out, and_4_out, and_5_out, and_6_out, and_7_out, not_1_out, not_2_out,
       not_3_out;

  not not_1 (not_1_out, in_1);
  not not_2 (not_2_out, in_2);
  not not_3 (not_3_out, in_3);
  and and_1 (and_1_out, not_3_out, not_2_out, in_1);
  and and_2 (and_2_out, not_1_out, in_2, in_3);
  and and_3 (and_3_out, in_1, not_2_out, in_3);
  and and_4 (and_4_out, not_1_out, in_2, not_3_out);
  and and_5 (and_5_out, in_1, in_2, not_3_out);
  and and_6 (and_6_out, in_1, in_2, in_3);
  and and_7 (and_7_out, not_2_out, not_1_out, in_3);
  or or_1 (Flan_Droit, and_4_out, and_7_out);
  or or_2 (Random, and_2_out, and_3_out, and_5_out, and_6_out);
  or or_3 (Flan_gauche, and_1_out, and_4_out);

  // Notes on the sheet:
  //   Droit
  //   Centre
  //   Gauche
endmodule
