// Logisim project Schéma_logique_4_capteurs.circ as structural Verilog: 1 circuit, main circuit main
module main (
  input  gauche,
  input  c_g,
  input  c_d,
  input  droite,
  output Flan_droit,
  output out_6,
  output Flan_gauche
);

  wire and_1_out, and_2_out, and_3_out, and_4_out, and_5_out, and_6_out, and_7_out, and_8_out, and_9_out,
       and_10_out, and_11_out, and_12_out, and_13_out, and_14_out, and_15_out, not_1_out, not_2_out,
       not_3_out, not_4_out, or_3_out;

  or or_1 (Flan_droit, and_1_out, or_3_out);
  or or_2 (Flan_gauche, or_3_out, and_5_out);
  or or_3 (or_3_out, and_2_out, and_3_out, and_4_out);
  and and_1 (and_1_out, gauche, not_2_out, not_3_out, not_4_out);
  and and_2 (and_2_out, not_1_out, c_g, not_3_out, not_4_out);
  and and_3 (and_3_out, not_1_out, not_2_out, c_d, not_4_out);
  and and_4 (and_4_out, not_1_out, c_g, c_d, not_4_out);
  and and_5 (and_5_out, not_1_out, not_2_out, not_3_out, droite);
  not not_1 (not_1_out, gauche);
  not not_2 (not_2_out, c_g);
  not not_3 (not_3_out, c_d);
  not not_4 (not_4_out, droite);
  and and_6 (and_6_out, droite, c_d, not_2_out, not_1_out);
  and and_7 (and_7_out, droite, not_3_out, c_g, not_1_out);
  and and_8 (and_8_out, droite, c_d, c_g, not_1_out);
  and and_9 (and_9_out, droite, not_3_out, not_2_out, gauche);
  and and_10 (and_10_out, not_4_out, c_d, not_2_out, gauche);
  and and_11 (and_11_out, droite, c_d, not_2_out, gauche);
  and and_12 (and_12_out, not_4_out, not_3_out, c_g, gauche);
  and and_13 (and_13_out, droite, not_3_out, gauche, gauche);
  and and_14 (and_14_out, not_4_out, c_g, c_g, gauche);
  and and_15 (and_15_out, droite, c_d, c_g, gauche);
  or or_4 (out_6, and_6_out, and_7_out, and_8_out, and_9_out, and_10_out, and_11_out, and_12_out, and_13_out, and_14_out, and_15_out);

  // Notes on the sheet:
  //   Random
endmodule
